# Fritzing sketch wakeon_pc (saved by Fritzing 0.9.3b)
circuit board: 6.09195cm x 3.32871cm
breadboards: 1

parts:
  ESP8266 = WeMos D1 Mini
  U2_Optopkoppler = TLP621 [package=THT]
  U3_Optokoppler = TLP621 [package=THT]
  R1 = Resistor [tolerance=±5% resistance=330 package=THT]
  R2 = Resistor [tolerance=±5% resistance=330 package=THT]
  J3 = male pin header, 2 pins [form="♂ (male)"]
  J2 = male pin header, 2 pins [form="♂ (male)"]
  J4 = male pin header, 2 pins [form="♂ (male)"]
  J1 = male pin header, 2 pins [form="♂ (male)"]

nets:
  N1: ESP8266.D7, U2_Optopkoppler.Pin_1
  N2: ESP8266.D8, U3_Optokoppler.Pin_1
  N3: ESP8266.G, R1.Pin_0, R2.Pin_0
  N4: U2_Optopkoppler.Pin_2, R1.Pin_1
  N5: U2_Optopkoppler.Pin_4, J2.pin2, J1.pin2
  N6: U2_Optopkoppler.Pin_3, J2.pin1, J1.pin1
  N7: U3_Optokoppler.Pin_2, R2.Pin_1
  N8: U3_Optokoppler.Pin_4, J3.pin2, J4.pin2
  N9: U3_Optokoppler.Pin_3, J3.pin1, J4.pin1
